// Digital circuit alu.dig as structural Verilog
module alu (
  input  [7:0] b,
  input  [7:0] a,
  input  [1:0] op,
  output [7:0] s,
  output c,
  output z
);

  wire add, \and , or_1_out, sub, \xor ;
  wire [7:0] add_1_s, and_1_out, bitextender_1_out, xor_1_out, xor_2_out;

  BitExtender #(.inputBits(1), .outputBits(8)) bitextender_1 (.in(sub), .out(bitextender_1_out));
  assign xor_1_out = b ^ bitextender_1_out;  // XOr xor_1, 8 bits wide
  Decoder #(.Selector_Bits(2)) decoder_1 (.sel(op), .out_0(add), .out_1(sub), .out_2(\and ), .out_3(\xor ));
  Add #(.Bits(8)) add_1 (.a(a), .b(xor_1_out), .c_i(sub), .s(add_1_s), .c_o(c));
  assign xor_2_out = a ^ b;  // XOr xor_2, 8 bits wide
  assign and_1_out = a & b;  // And and_1, 8 bits wide
  or or_1 (or_1_out, sub, add);
  assign s = or_1_out ? add_1_s : 8'bz;  // Driver driver_1
  assign s = \xor  ? xor_2_out : 8'bz;  // Driver driver_2
  assign s = \and  ? and_1_out : 8'bz;  // Driver driver_3
  nor nor_1 (z, s[0], s[1], s[2], s[3], s[4], s[5], s[6], s[7]);
endmodule
