// Digital circuit computah.dig as structural Verilog
module computah (
  input  clk
);

  wire demultiplexer_1_out_0, demultiplexer_1_out_1, demultiplexer_1_out_2, demultiplexer_1_out_3,
       demultiplexer_1_out_4, demultiplexer_1_out_5, demultiplexer_1_out_6, demultiplexer_1_out_7,
       demultiplexer_1_out_8, demultiplexer_1_out_9, demultiplexer_1_out_10, demultiplexer_1_out_11,
       demultiplexer_1_out_12, demultiplexer_1_out_13, demultiplexer_1_out_14, demultiplexer_2_out_1,
       demultiplexer_2_out_2, demultiplexer_2_out_3, demultiplexer_2_out_4, demultiplexer_2_out_5,
       demultiplexer_2_out_6, demultiplexer_2_out_7, demultiplexer_2_out_8, demultiplexer_2_out_9,
       demultiplexer_2_out_10, demultiplexer_2_out_11, demultiplexer_2_out_12, demultiplexer_2_out_13,
       demultiplexer_2_out_14, io_oe, io_we, kb_oe, keyboard_1_av, m_oe, m_we, ram_oe, ram_we, rom_oe, tm_we;
  wire [3:0] sel;
  wire [7:0] d;
  wire [11:0] addr;
  wire [15:8] keyboard_1_d;

  RAMDualPort #(.AddrBits(12), .Bits(8)) ramdualport_1 (.A(addr), .Din(d), .str(ram_we), .C(clk), .ld(ram_oe), .D(d));
  ROM #(.AddrBits(12), .Bits(8)) rom_1 (.A(addr), .sel(rom_oe), .D(d));
  Keyboard keyboard_1 (.C(clk), .en(kb_oe), .D({keyboard_1_d, d}), .av(keyboard_1_av));
  Terminal terminal_1 (.D(d), .C(clk), .en(tm_we));
  // Probe on {keyboard_1_d, d}
  LED led_1 (.in(keyboard_1_av));
  // Probe on d
  // Probe on addr
  LED led_2 (.in(rom_oe));
  LED led_3 (.in(ram_oe));
  // main main_1: pin names not known; wires that end beside it: clk, d, {sel, addr}, m_we, m_oe
  LED led_4 (.in(demultiplexer_1_out_14));
  LED led_5 (.in(demultiplexer_1_out_13));
  LED led_6 (.in(demultiplexer_1_out_12));
  LED led_7 (.in(demultiplexer_1_out_11));
  or or_1 (ram_we, demultiplexer_1_out_1, demultiplexer_1_out_2, demultiplexer_1_out_3, demultiplexer_1_out_4, demultiplexer_1_out_5, demultiplexer_1_out_6, demultiplexer_1_out_7, demultiplexer_1_out_8, demultiplexer_1_out_9, demultiplexer_1_out_10);
  LED led_8 (.in(demultiplexer_1_out_0));
  LED led_9 (.in(demultiplexer_2_out_14));
  LED led_10 (.in(demultiplexer_2_out_13));
  LED led_11 (.in(demultiplexer_2_out_12));
  LED led_12 (.in(demultiplexer_2_out_11));
  or or_2 (ram_oe, demultiplexer_2_out_1, demultiplexer_2_out_2, demultiplexer_2_out_3, demultiplexer_2_out_4, demultiplexer_2_out_5, demultiplexer_2_out_6, demultiplexer_2_out_7, demultiplexer_2_out_8, demultiplexer_2_out_9, demultiplexer_2_out_10);
  LED led_13 (.in(kb_oe));
  Demultiplexer #(.Selector_Bits(4)) demultiplexer_1 (
    .sel(sel), .in(m_we), .out_0(demultiplexer_1_out_0), .out_1(demultiplexer_1_out_1),
    .out_2(demultiplexer_1_out_2), .out_3(demultiplexer_1_out_3), .out_4(demultiplexer_1_out_4),
    .out_5(demultiplexer_1_out_5), .out_6(demultiplexer_1_out_6), .out_7(demultiplexer_1_out_7),
    .out_8(demultiplexer_1_out_8), .out_9(demultiplexer_1_out_9), .out_10(demultiplexer_1_out_10),
    .out_11(demultiplexer_1_out_11), .out_12(demultiplexer_1_out_12), .out_13(demultiplexer_1_out_13),
    .out_14(demultiplexer_1_out_14), .out_15(io_we));
  Demultiplexer #(.Selector_Bits(4)) demultiplexer_2 (
    .sel(sel), .in(m_oe), .out_0(rom_oe), .out_1(demultiplexer_2_out_1), .out_2(demultiplexer_2_out_2),
    .out_3(demultiplexer_2_out_3), .out_4(demultiplexer_2_out_4), .out_5(demultiplexer_2_out_5),
    .out_6(demultiplexer_2_out_6), .out_7(demultiplexer_2_out_7), .out_8(demultiplexer_2_out_8),
    .out_9(demultiplexer_2_out_9), .out_10(demultiplexer_2_out_10), .out_11(demultiplexer_2_out_11),
    .out_12(demultiplexer_2_out_12), .out_13(demultiplexer_2_out_13), .out_14(demultiplexer_2_out_14),
    .out_15(io_oe));
  Demultiplexer #(.Selector_Bits(4)) demultiplexer_3 (
    .sel(addr[3:0]), .in(io_we), .out_1(tm_we));  // open: out_0, out_2, out_3, out_4, out_5, out_6, out_7, out_8, out_9, out_10, out_11, out_12, out_13, out_14, out_15
  Demultiplexer #(.Selector_Bits(4)) demultiplexer_4 (
    .sel(addr[3:0]), .in(io_oe), .out_0(kb_oe));  // open: out_1, out_2, out_3, out_4, out_5, out_6, out_7, out_8, out_9, out_10, out_11, out_12, out_13, out_14, out_15

  // Other names for the same wires on the sheet: c = clk

  // Notes on the sheet:
  //   clk: Hz: 100
  //   contents of rom_1 (hex, n*v repeats v):
  //   40,10,50,0,40,0,60,0,40,2,80,0,c0,58,40,11,50,0,40,10,60,0,70
  //   ,0,90,0,b0,0,70,0,50,0,40,0,0,0,60,0,40,f0,95,0,40,1,96,0,40,0
  //   ,90,0,70,0,10,0,e0,3e,93,0,b0,0,c0,2e,40,11,50,0,40,0,60,0,70
  //   ,0,90,0,b0,0,70,0,50,0,40,0,0,0,60,0,d0,0,40,f0,50,0,40,0,60,0
  //   ,70,0,90,0,40,0,10,0,e0,58,40,10,50,0,40,1,60,0,40,0,0,0,80,0
  //   ,40,a,10,0,e1,0,40,8,10,0,e0,ce,40,10,50,0,40,0,60,0,70,0,90,0
  //   ,40,ff,10,0,e0,58,40,1,60,0,70,0,90,0,40,0,60,0,70,0,60,0,40,0,0,0
  //   ,80,0,40,f0,50,0,40,1,60,0,40,0,0,0,80,0,40,10,50,0,40,0,60,0
  //   ,70,0,90,0,40,1,0,0,80,0,c0,58,40,2,90,0,40,10,50,0,40,0,60,0
  //   ,70,0,10,0,e0,58,40,1,90,0,70,0,10,0,80,0,40,f0,50,0,40,1,60,0
  //   ,40,8,80,0,40,20,80,0,40,8,80,0,c0,58,40,f0,50,0,40,1,60,0,40
  //   ,d,80,0,40,a,80,0,40,10,50,0,40,0,60,0,70,0,90,0,40,2,10,0,e1
  //   ,24,c1,32,40,10,50,0,40,0,60,0,40,2,80,0,c0,58,40,10,50,0,40,1
  //   ,60,0,70,0,90,0,c1,51,55,6e,6b,6e,6f,77,6e,20,43,6f,6d,6d,61,6e
  //   ,64,21,0,40,11,50,0,40,10,60,0,40,40,80,0,b0,0,40,1,80,0,40,0
  //   ,60,0,40,73,80,0,b0,0,40,1,80,0,c0,e,c1,24
endmodule
