// Digital circuit decoder.dig as structural Verilog
module decoder (
  input  [7:0] b0,
  input  [7:0] b1,
  output [3:0] op,
  output [11:0] imm_12,
  output [7:0] imm_8
);


  assign imm_8 = b1;
  assign imm_12 = {b0[3:0], b1};
  assign op = b0[7:4];
endmodule
