// Digital circuit main.dig as structural Verilog
module main (
  input  [7:0] D_in,
  input  C,
  output [15:0] A_bus,
  output m_we,
  output m_oe
);

  wire addr_pc, addr_uv, addr_xy, and_1_out, bus_transceiver_1_p1, carry, clk_v, clk_y, cond, cond_upc_clr,
       dst_a, dst_b, dst_u, dst_v, dst_x, dst_y, f_c, f_z, flags_we, ir0_rd, ir1_rd, multiplexer_1_out,
       not_1_out, or_1_out, or_2_out, pc_imm, pc_inc, pc_rd, pc_uv, pc_xy, src_a, src_alu, src_b,
       src_external, src_imm8, src_shr, src_u, src_v, src_x, src_y, upc_clr, V_ovf, Y_ovf, zero;
  wire [1:0] alu_op, pc_src, src_addr, uPC_out;
  wire [2:0] dst_data;
  wire [3:0] src_data;
  wire [3:2] op;
  wire [7:0] a_cont, alu_1_s, b_cont, driver_7_out, imm8, register_1_q, register_2_q;
  wire [7:6] rom_3_d;
  wire [11:0] imm12;
  wire [15:0] driver_1_out, pc_content, UV, XY;

  and and_1 (and_1_out, not_1_out, cond_upc_clr);
  not not_1 (not_1_out, cond);
  Decoder #(.Selector_Bits(2)) decoder_1 (.sel(pc_src), .out_0(pc_xy), .out_1(pc_uv), .out_2(pc_imm));  // open: out_3
  or or_1 (or_1_out, and_1_out, upc_clr);
  Counter #(.Bits(2)) uPC (.en(1'b1), .C(C), .clr(or_1_out), .out(uPC_out));  // open: ovf
  ROM #(.AddrBits(18), .Bits(8)) rom_1 (.A({op, alu_op, imm12, uPC_out}), .sel(1'b1), .D({m_oe, dst_data, src_data}));
  ROM #(.AddrBits(18), .Bits(8)) rom_2 (
    .A({op, alu_op, imm12, uPC_out}), .sel(1'b1), .D({ir0_rd, pc_src, pc_rd, pc_inc, src_addr, m_we}));
  or or_2 (or_2_out, pc_rd, pc_inc);
  assign driver_1_out = pc_uv ? UV : 16'bz;  // Driver driver_1
  assign driver_1_out = pc_xy ? XY : 16'bz;  // Driver driver_2
  assign driver_1_out = pc_imm ? {pc_content[15:12], imm12} : 16'bz;  // Driver driver_3
  Decoder #(.Selector_Bits(4)) decoder_2 (
    .sel(src_data), .out_1(src_a), .out_2(src_b), .out_3(src_x), .out_4(src_y), .out_5(src_u), .out_6(src_v),
    .out_7(src_alu), .out_8(src_shr), .out_9(src_imm8), .out_10(src_external));  // open: out_0, out_11, out_12, out_13, out_14, out_15
  CounterPreset #(.Bits(16)) PC (
    .en(or_2_out), .C(C), .dir(1'b0), .in(driver_1_out), .ld(pc_rd), .clr(1'b0), .out(pc_content));  // open: ovf
  ROM #(.AddrBits(18), .Bits(8)) rom_3 (
    .A({op, alu_op, imm12, uPC_out}), .sel(1'b1),
    .D({rom_3_d, cond_upc_clr, upc_clr, flags_we, clk_v, clk_y, ir1_rd}));
  Decoder #(.Selector_Bits(2)) decoder_3 (
    .sel(src_addr), .out_0(addr_pc), .out_1(addr_xy), .out_2(addr_uv));  // open: out_3
  assign A_bus = addr_pc ? pc_content : 16'bz;  // Driver driver_4
  assign A_bus = addr_xy ? XY : 16'bz;  // Driver driver_5
  Decoder #(.Selector_Bits(3)) decoder_4 (
    .sel(dst_data), .out_1(dst_a), .out_2(dst_b), .out_3(dst_x), .out_4(dst_y), .out_5(dst_u), .out_6(dst_v));  // open: out_0, out_7
  assign A_bus = addr_uv ? UV : 16'bz;  // Driver driver_6
  CounterPreset #(.Bits(8)) V (
    .en(clk_v), .C(C), .dir(1'b0), .in(driver_7_out), .ld(dst_v), .clr(1'b0), .out(UV[7:0]), .ovf(V_ovf));
  CounterPreset #(.Bits(8)) U (
    .en(V_ovf), .C(C), .dir(1'b0), .in(driver_7_out), .ld(dst_u), .clr(1'b0), .out(UV[15:8]));  // open: ovf
  decoder decoder_5 (.b0(register_2_q), .b1(register_1_q), .op({op, alu_op}), .imm_12(imm12), .imm_8(imm8));
  Register #(.Bits(8)) register_1 (.D(driver_7_out), .C(C), .en(ir1_rd), .Q(register_1_q));
  Register #(.Bits(8)) register_2 (.D(driver_7_out), .C(C), .en(ir0_rd), .Q(register_2_q));
  assign driver_7_out = src_v ? UV[7:0] : 8'bz;  // Driver driver_7
  assign driver_7_out = src_u ? UV[15:8] : 8'bz;  // Driver driver_8
  // bus_transceiver bus_transceiver_1: pin names not known; wires that end beside it: bus_transceiver_1_p1, 1'b0, driver_7_out, D_in
  not not_2 (bus_transceiver_1_p1, src_external);
  assign driver_7_out = src_a ? a_cont : 8'bz;  // Driver driver_9
  assign driver_7_out = src_b ? b_cont : 8'bz;  // Driver driver_10
  assign driver_7_out = src_x ? XY[15:8] : 8'bz;  // Driver driver_11
  assign driver_7_out = src_y ? XY[7:0] : 8'bz;  // Driver driver_12
  assign driver_7_out = src_imm8 ? imm8 : 8'bz;  // Driver driver_13
  Register #(.Bits(8)) A (.D(driver_7_out), .C(C), .en(dst_a), .Q(a_cont));
  Register #(.Bits(8)) B (.D(driver_7_out), .C(C), .en(dst_b), .Q(b_cont));
  CounterPreset #(.Bits(8)) X (
    .en(Y_ovf), .C(C), .dir(1'b0), .in(driver_7_out), .ld(dst_x), .clr(1'b0), .out(XY[15:8]));  // open: ovf
  CounterPreset #(.Bits(8)) Y (
    .en(clk_y), .C(C), .dir(1'b0), .in(driver_7_out), .ld(dst_y), .clr(1'b0), .out(XY[7:0]), .ovf(Y_ovf));
  assign driver_7_out = src_alu ? alu_1_s : 8'bz;  // Driver driver_14
  assign driver_7_out = src_shr ? {1'b0, a_cont[7:1]} : 8'bz;  // Driver driver_15
  Multiplexer multiplexer_1 (.sel(src_shr), .in_0(carry), .in_1(a_cont[0]), .out(multiplexer_1_out));
  Multiplexer multiplexer_2 (.sel(alu_op[0]), .in_0(f_z), .in_1(f_c), .out(cond));
  alu alu_1 (.b(b_cont), .a(a_cont), .op(alu_op), .s(alu_1_s), .c(carry), .z(zero));
  D_FF d_ff_1 (.D(zero), .C(flags_we), .Q(f_z));  // open: nQ
  D_FF d_ff_2 (.D(multiplexer_1_out), .C(flags_we), .Q(f_c));  // open: nQ

  // Other names for the same wires on the sheet: mem_oe = m_oe; mem_we = m_we; shr_c = a_cont[0]; op[1:0] = alu_op

  // Notes on the sheet:
  //   C: Hz: 10
  //   Microcode
  //   PC & Address Bus
  //   contents of rom_1 (hex, n*v repeats v):
  //   8a,8a,17,0,8a,8a,17,0,8a,8a,17,0,8a,8a,17,0,8a,8a,17,0,8a,8a,17
  //   ,0,8a,8a,17,0,8a,8a,17,0,8a,8a,17,0,8a,8a,17,0,8a,8a,17,0,8a,8a
  //   ,17,0,8a,8a,17,0,8a,8a,17,0,8a,8a,17,0,8a,8a,17,0,8a,8a,17,0,8a,8a
  //   ,17,0,8a,8a,17,0,8a,8a,17,0,8a,8a,17,0,8a,8a,17,0,8a,8a,17,0,8a,8a
  //   ,17,0,8a,8a,17,0,8a,8a,17,0,8a,8a,17,0,8a,8a,17,0,8a,8a,17,0,8a,8a
  //   ,17,0,8a,8a,17,0,8a,8a,17,0,8a,8a,17,0,8a,8a,17,0,8a,8a,17,0,8a,8a
  //   ,17,0,8a,8a,17,0,8a,8a,17,0,8a,8a,17,0,8a,8a,17,0,8a,8a,17,0,8a,8a
  //   ,17,0,8a,8a,17,0,8a,8a,17,0,8a,8a,17,0,8a,8a,17,0,8a,8a,17,0,8a,8a
  //   ,17,0,8a,8a,17,0,8a,8a,17,0,8a,8a,17,0,8a,8a,17,0,8a,8a,17,0,8a,8a
  //   ,17,0,8a,8a,17,0,8a,8a,17,0,8a,8a,17,0,8a,8a,17,0,8a,8a,17,0,8a,8a
  //   ,17,0,8a,8a,17,0,8a,8a,17,0,8a,8a,17,0,8a,8a,17,0,8a,8a,17,0,8a,8a
  //   ,17,0,8a,8a,17,0,8a,8a,17,0,8a,8a,17,0,8a,8a,17,0,8a,8a,17,0,8a,8a
  //   ,17,0,8a,8a,17,0,8a,8a,17,0,8a,8a,17,0,8a,8a,17,0,8a,8a,17,0,8a,8a
  //   ,17,0,8a,8a,17,0,8a,8a,17,0,8a,8a,17,0,8a,8a,17,0,8a,8a,17,0,8a,8a
  //   ,17,0,8a,8a,17,0,8a,8a,17,0,8a,8a,17,0,8a,8a,17,0,8a,8a,17,0,8a,8a
  //   ,17,0,8a,8a,17,0,8a,8a,17,0,8a,8a,17,0,8a,8a,17,0,8a,8a,17,0,8a,8a
  //   ,17,0,8a,8a,17,0,8a,8a,17,0,8a,8a,17,0,8a,8a,17,0,8a,8a,17,0,8a,8a
  //   ,17,0,8a,8a,17,0,8a,8a,17,0,8a,8a,17,0,8a,8a,17,0,8a,8a,17,0,8a,8a
  //   ,17,0,8a,8a,17,0,8a,8a,17,0,8a,8a,17,0,8a,8a,17,0,8a,8a,17,0,8a,8a
  //   ,17,0,8a,8a,17,0,8a,8a,17,0,8a,8a,17,0,8a,8a,17,0,8a,8a,17,0,8a,8a
  //   ,17,0,8a,8a,17,0,8a,8a,17,0,8a,8a,17,0,8a,8a,17,0,8a,8a,17,0,8a,8a
  //   ,17,0,8a,8a,17,0,8a,8a,17,0,8a,8a,17,0,8a,8a,17,0,8a,8a,17,0,8a,8a
  //   ,17,0,8a,8a,17,0,8a,8a,17,0,8a,8a,17,0,8a,8a,17,0,8a,8a,17,0,8a,8a
  //   ,17,0,8a,8a,17,0,8a,8a,17,0,8a,8a,17,0,8a,8a,17,0,8a,8a,17,0,8a,8a
  //   ,17,0,8a,8a,17,0,8a,8a,17,0,8a,8a,17,0,8a,8a,17,0,8a,8a,17,0,8a,8a
  //   ,17,0,8a,8a,17,0,8a,8a,17,0,8a,8a,17,0,8a,8a,17,0,8a,8a,17,0,8a,8a
  //   ,17,0,8a,8a,17,0,8a,8a,17,0,8a,8a,17,0,8a,8a,17,0,8a,8a,17,0,8a,8a
  //   ,17,0,8a,8a,17,0,8a,8a,17,0,8a,8a,17,0,8a,8a,17,0,8a,8a,17,0,8a,8a
  //   ,17,0,8a,8a,17,0,8a,8a,17,0,8a,8a,17,0,8a,8a,17,0,8a,8a,17,0,8a,8a
  //   ,17,0,8a,8a,17,0,8a,8a,17,0,8a,8a,17,0,8a,8a,17,0,8a,8a,17,0,8a,8a
  //   ,17,0,8a,8a,17,0,8a,8a,17,0,8a,8a,17,0,8a,8a,17,0,8a,8a,17,0,8a,8a
  //   ,17,0,8a,8a,17,0,8a,8a,17,0,8a,8a,17,0,8a,8a,17,0,8a,8a,17,0,8a,8a
  //   ,17,0,8a,8a,17,0,8a,8a,17,0,8a,8a,17,0,8a,8a,17,0,8a,8a,17,0,8a,8a
  //   ,17,0,8a,8a,17,0,8a,8a,17,0,8a,8a,17,0,8a,8a,17,0,8a,8a,17,0,8a,8a
  //   ,17,0,8a,8a,17,0,8a,8a,17,0,8a,8a,17,0,8a,8a,17,0,8a,8a,17,0,8a,8a
  //   ,17,0,8a,8a,17,0,8a,8a,17,0,8a,8a,17,0,8a,8a,17,0,8a,8a,17,0,8a,8a
  //   ,17,0,8a,8a,17,0,8a,8a,17,0,8a,8a,17,0,8a,8a,17,0,8a,8a,17,0,8a,8a
  //   ,17,0,8a,8a,17,0,8a,8a,17,0,8a,8a,17,0,8a,8a,17,0,8a,8a,17,0,8a,8a
  //   ,17,0,8a,8a,17,0,8a,8a,17,0,8a,8a,17,0,8a,8a,17,0,8a,8a,17,0,8a,8a
  //   ,17,0,8a,8a,17,0,8a,8a,17,0,8a,8a,17,0,8a,8a,17,0,8a,8a,17,0,8a,8a
  //   ,17,0,8a,8a,17,0,8a,8a,17,0,8a,8a,17,0,8a,8a,17,0,8a,8a,17,0,8a,8a
  //   ,17,0,8a,8a,17,0,8a,8a,17,0,8a,8a,17,0,8a,8a,17,0,8a,8a,17,0,8a,8a
  //   ,17,0,8a,8a,17,0,8a,8a,17,0,8a,8a,17,0,8a,8a,17,0,8a,8a,17,0,8a,8a
  //   ,17,0,8a,8a,17,0,8a,8a,17,0,8a,8a,17,0,8a,8a,17,0,8a,8a,17,0,8a,8a
  //   ,17,0,8a,8a,17,0,8a,8a,17,0,8a,8a,17,0,8a,8a,17,0,8a,8a,17,0,8a,8a
  //   ,17,0,8a,8a,17,0,8a,8a,17,0,8a,8a,17,0,8a,8a,17,0,8a,8a,17,0,8a,8a
  //   ,17,0,8a,8a,17,0,8a,8a,17,0,8a,8a,17,0,8a,8a,17,0,8a,8a,17,0,8a,8a
  //   ,17,0,8a,8a,17,0,8a,8a,17,0,8a,8a,17,0,8a,8a,17,0,8a,8a,17,0,8a,8a
  //   ,17,0,8a,8a,17,0,8a,8a,17,0,8a,8a,17,0,8a,8a,17,0,8a,8a,17,0,8a,8a
  //   ,17,0,8a,8a,17,0,8a,8a,17,0,8a,8a,17,0,8a,8a,17,0,8a,8a,17,0,8a,8a
  //   ,17,0,8a,8a,17,0,8a,8a,17,0,8a,8a,17,0,8a,8a,17,0,8a,8a,17,0,8a,8a
  //   ,17,0,8a,8a,17,0,8a,8a,17,0,8a,8a,17,0,8a,8a,17,0,8a,8a,17,0,8a,8a
  //   ,17,0,8a,8a,17,0,8a,8a,17,0,8a,8a,17,0,8a,8a,17,0,8a,8a,17,0,8a,8a
  //   ,17,0,8a,8a,17,0,8a,8a,17,0,8a,8a,17,0,8a,8a,17,0,8a,8a,17,0,8a,8a
  //   ,17,0,8a,8a,17,0,8a,8a,17,0,8a,8a,17,0,8a,8a,17,0,8a,8a,17,0,8a,8a
  //   ,17,0,8a,8a,17,0,8a,8a,17,0,8a,8a,17,0,8a,8a,17,0,8a,8a,17,0,8a,8a
  //   ,17,0,8a,8a,17,0,8a,8a,17,0,8a,8a,17,0,8a,8a,17,0,8a,8a,17,0,8a,8a
  //   ,17,0,8a,8a,17,0,8a,8a,17,0,8a,8a,17,0,8a,8a,17,0,8a,8a,17,0,8a,8a
  //   ,17,0,8a,8a,17,0,8a,8a,17,0,8a,8a,17,0,8a,8a,17,0,8a,8a,17,0,8a,8a
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  //   contents of rom_2 (hex, n*v repeats v):
  //   88,8,0,0,88,8,0,0,88,8,0,0,88,8,0,0,88,8,0,0,88,8,0,0,88,8,0,0
  //   ,88,8,0,0,88,8,0,0,88,8,0,0,88,8,0,0,88,8,0,0,88,8,0,0,88,8,0,0
  //   ,88,8,0,0,88,8,0,0,88,8,0,0,88,8,0,0,88,8,0,0,88,8,0,0,88,8,0,0
  //   ,88,8,0,0,88,8,0,0,88,8,0,0,88,8,0,0,88,8,0,0,88,8,0,0,88,8,0,0
  //   ,88,8,0,0,88,8,0,0,88,8,0,0,88,8,0,0,88,8,0,0,88,8,0,0,88,8,0,0
  //   ,88,8,0,0,88,8,0,0,88,8,0,0,88,8,0,0,88,8,0,0,88,8,0,0,88,8,0,0
  //   ,88,8,0,0,88,8,0,0,88,8,0,0,88,8,0,0,88,8,0,0,88,8,0,0,88,8,0,0
  //   ,88,8,0,0,88,8,0,0,88,8,0,0,88,8,0,0,88,8,0,0,88,8,0,0,88,8,0,0
  //   ,88,8,0,0,88,8,0,0,88,8,0,0,88,8,0,0,88,8,0,0,88,8,0,0,88,8,0,0
  //   ,88,8,0,0,88,8,0,0,88,8,0,0,88,8,0,0,88,8,0,0,88,8,0,0,88,8,0,0
  //   ,88,8,0,0,88,8,0,0,88,8,0,0,88,8,0,0,88,8,0,0,88,8,0,0,88,8,0,0
  //   ,88,8,0,0,88,8,0,0,88,8,0,0,88,8,0,0,88,8,0,0,88,8,0,0,88,8,0,0
  //   ,88,8,0,0,88,8,0,0,88,8,0,0,88,8,0,0,88,8,0,0,88,8,0,0,88,8,0,0
  //   ,88,8,0,0,88,8,0,0,88,8,0,0,88,8,0,0,88,8,0,0,88,8,0,0,88,8,0,0
  //   ,88,8,0,0,88,8,0,0,88,8,0,0,88,8,0,0,88,8,0,0,88,8,0,0,88,8,0,0
  //   ,88,8,0,0,88,8,0,0,88,8,0,0,88,8,0,0,88,8,0,0,88,8,0,0,88,8,0,0
  //   ,88,8,0,0,88,8,0,0,88,8,0,0,88,8,0,0,88,8,0,0,88,8,0,0,88,8,0,0
  //   ,88,8,0,0,88,8,0,0,88,8,0,0,88,8,0,0,88,8,0,0,88,8,0,0,88,8,0,0
  //   ,88,8,0,0,88,8,0,0,88,8,0,0,88,8,0,0,88,8,0,0,88,8,0,0,88,8,0,0
  //   ,88,8,0,0,88,8,0,0,88,8,0,0,88,8,0,0,88,8,0,0,88,8,0,0,88,8,0,0
  //   ,88,8,0,0,88,8,0,0,88,8,0,0,88,8,0,0,88,8,0,0,88,8,0,0,88,8,0,0
  //   ,88,8,0,0,88,8,0,0,88,8,0,0,88,8,0,0,88,8,0,0,88,8,0,0,88,8,0,0
  //   ,88,8,0,0,88,8,0,0,88,8,0,0,88,8,0,0,88,8,0,0,88,8,0,0,88,8,0,0
  //   ,88,8,0,0,88,8,0,0,88,8,0,0,88,8,0,0,88,8,0,0,88,8,0,0,88,8,0,0
  //   ,88,8,0,0,88,8,0,0,88,8,0,0,88,8,0,0,88,8,0,0,88,8,0,0,88,8,0,0
  //   ,88,8,0,0,88,8,0,0,88,8,0,0,88,8,0,0,88,8,0,0,88,8,0,0,88,8,0,0
  //   ,88,8,0,0,88,8,0,0,88,8,0,0,88,8,0,0,88,8,0,0,88,8,0,0,88,8,0,0
  //   ,88,8,0,0,88,8,0,0,88,8,0,0,88,8,0,0,88,8,0,0,88,8,0,0,88,8,0,0
  //   ,88,8,0,0,88,8,0,0,88,8,0,0,88,8,0,0,88,8,0,0,88,8,0,0,88,8,0,0
  //   ,88,8,0,0,88,8,0,0,88,8,0,0,88,8,0,0,88,8,0,0,88,8,0,0,88,8,0,0
  //   ,88,8,0,0,88,8,0,0,88,8,0,0,88,8,0,0,88,8,0,0,88,8,0,0,88,8,0,0
  //   ,88,8,0,0,88,8,0,0,88,8,0,0,88,8,0,0,88,8,0,0,88,8,0,0,88,8,0,0
  //   ,88,8,0,0,88,8,0,0,88,8,0,0,88,8,0,0,88,8,0,0,88,8,0,0,88,8,0,0
  //   ,88,8,0,0,88,8,0,0,88,8,0,0,88,8,0,0,88,8,0,0,88,8,0,0,88,8,0,0
  //   ,88,8,0,0,88,8,0,0,88,8,0,0,88,8,0,0,88,8,0,0,88,8,0,0,88,8,0,0
  //   ,88,8,0,0,88,8,0,0,88,8,0,0,88,8,0,0,88,8,0,0,88,8,0,0,88,8,0,0
  //   ,88,8,0,0,88,8,0,0,88,8,0,0,88,8,0,0,88,8,0,0,88,8,0,0,88,8,0,0
  //   ,88,8,0,0,88,8,0,0,88,8,0,0,88,8,0,0,88,8,0,0,88,8,0,0,88,8,0,0
  //   ,88,8,0,0,88,8,0,0,88,8,0,0,88,8,0,0,88,8,0,0,88,8,0,0,88,8,0,0
  //   ,88,8,0,0,88,8,0,0,88,8,0,0,88,8,0,0,88,8,0,0,88,8,0,0,88,8,0,0
  //   ,88,8,0,0,88,8,0,0,88,8,0,0,88,8,0,0,88,8,0,0,88,8,0,0,88,8,0,0
  //   ,88,8,0,0,88,8,0,0,88,8,0,0,88,8,0,0,88,8,0,0,88,8,0,0,88,8,0,0
  //   ,88,8,0,0,88,8,0,0,88,8,0,0,88,8,0,0,88,8,0,0,88,8,0,0,88,8,0,0
  //   ,88,8,0,0,88,8,0,0,88,8,0,0,88,8,0,0,88,8,0,0,88,8,0,0,88,8,0,0
  //   ,88,8,0,0,88,8,0,0,88,8,0,0,88,8,0,0,88,8,0,0,88,8,0,0,88,8,0,0
  //   ,88,8,0,0,88,8,0,0,88,8,0,0,88,8,0,0,88,8,0,0,88,8,0,0,88,8,0,0
  //   ,88,8,0,0,88,8,0,0,88,8,0,0,88,8,0,0,88,8,0,0,88,8,0,0,88,8,0,0
  //   ,88,8,0,0,88,8,0,0,88,8,0,0,88,8,0,0,88,8,0,0,88,8,0,0,88,8,0,0
  //   ,88,8,0,0,88,8,0,0,88,8,0,0,88,8,0,0,88,8,0,0,88,8,0,0,88,8,0,0
  //   ,88,8,0,0,88,8,0,0,88,8,0,0,88,8,0,0,88,8,0,0,88,8,0,0,88,8,0,0
  //   ,88,8,0,0,88,8,0,0,88,8,0,0,88,8,0,0,88,8,0,0,88,8,0,0,88,8,0,0
  //   ,88,8,0,0,88,8,0,0,88,8,0,0,88,8,0,0,88,8,0,0,88,8,0,0,88,8,0,0
  //   ,88,8,0,0,88,8,0,0,88,8,0,0,88,8,0,0,88,8,0,0,88,8,0,0,88,8,0,0
  //   ,88,8,0,0,88,8,0,0,88,8,0,0,88,8,0,0,88,8,0,0,88,8,0,0,88,8,0,0
  //   ,88,8,0,0,88,8,0,0,88,8,0,0,88,8,0,0,88,8,0,0,88,8,0,0,88,8,0,0
  //   ,88,8,0,0,88,8,0,0,88,8,0,0,88,8,0,0,88,8,0,0,88,8,0,0,88,8,0,0
  //   ,88,8,0,0,88,8,0,0,88,8,0,0,88,8,0,0,88,8,0,0,88,8,0,0,88,8,0,0
  //   ,88,8,0,0,88,8,0,0,88,8,0,0,88,8,0,0,88,8,0,0,88,8,0,0,88,8,0,0
  //   ,88,8,0,0,88,8,0,0,88,8,0,0,88,8,0,0,88,8,0,0,88,8,0,0,88,8,0,0
  //   ,88,8,0,0,88,8,0,0,88,8,0,0,88,8,0,0,88,8,0,0,88,8,0,0,88,8,0,0
  //   ,88,8,0,0,88,8,0,0,88,8,0,0,88,8,0,0,88,8,0,0,88,8,0,0,88,8,0,0
  //   ,88,8,0,0,88,8,0,0,88,8,0,0,88,8,0,0,88,8,0,0,88,8,0,0,88,8,0,0
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  //   contents of rom_3 (hex, n*v repeats v):
  //   0,1,18,10,0,1,18,10,0,1,18,10,0,1,18,10,0,1,18,10,0,1,18,10,0
  //   ,1,18,10,0,1,18,10,0,1,18,10,0,1,18,10,0,1,18,10,0,1,18,10,0,1
  //   ,18,10,0,1,18,10,0,1,18,10,0,1,18,10,0,1,18,10,0,1,18,10,0,1,18
  //   ,10,0,1,18,10,0,1,18,10,0,1,18,10,0,1,18,10,0,1,18,10,0,1,18,10
  //   ,0,1,18,10,0,1,18,10,0,1,18,10,0,1,18,10,0,1,18,10,0,1,18,10,0
  //   ,1,18,10,0,1,18,10,0,1,18,10,0,1,18,10,0,1,18,10,0,1,18,10,0,1
  //   ,18,10,0,1,18,10,0,1,18,10,0,1,18,10,0,1,18,10,0,1,18,10,0,1,18
  //   ,10,0,1,18,10,0,1,18,10,0,1,18,10,0,1,18,10,0,1,18,10,0,1,18,10
  //   ,0,1,18,10,0,1,18,10,0,1,18,10,0,1,18,10,0,1,18,10,0,1,18,10,0
  //   ,1,18,10,0,1,18,10,0,1,18,10,0,1,18,10,0,1,18,10,0,1,18,10,0,1
  //   ,18,10,0,1,18,10,0,1,18,10,0,1,18,10,0,1,18,10,0,1,18,10,0,1,18
  //   ,10,0,1,18,10,0,1,18,10,0,1,18,10,0,1,18,10,0,1,18,10,0,1,18,10
  //   ,0,1,18,10,0,1,18,10,0,1,18,10,0,1,18,10,0,1,18,10,0,1,18,10,0
  //   ,1,18,10,0,1,18,10,0,1,18,10,0,1,18,10,0,1,18,10,0,1,18,10,0,1
  //   ,18,10,0,1,18,10,0,1,18,10,0,1,18,10,0,1,18,10,0,1,18,10,0,1,18
  //   ,10,0,1,18,10,0,1,18,10,0,1,18,10,0,1,18,10,0,1,18,10,0,1,18,10
  //   ,0,1,18,10,0,1,18,10,0,1,18,10,0,1,18,10,0,1,18,10,0,1,18,10,0
  //   ,1,18,10,0,1,18,10,0,1,18,10,0,1,18,10,0,1,18,10,0,1,18,10,0,1
  //   ,18,10,0,1,18,10,0,1,18,10,0,1,18,10,0,1,18,10,0,1,18,10,0,1,18
  //   ,10,0,1,18,10,0,1,18,10,0,1,18,10,0,1,18,10,0,1,18,10,0,1,18,10
  //   ,0,1,18,10,0,1,18,10,0,1,18,10,0,1,18,10,0,1,18,10,0,1,18,10,0
  //   ,1,18,10,0,1,18,10,0,1,18,10,0,1,18,10,0,1,18,10,0,1,18,10,0,1
  //   ,18,10,0,1,18,10,0,1,18,10,0,1,18,10,0,1,18,10,0,1,18,10,0,1,18
  //   ,10,0,1,18,10,0,1,18,10,0,1,18,10,0,1,18,10,0,1,18,10,0,1,18,10
  //   ,0,1,18,10,0,1,18,10,0,1,18,10,0,1,18,10,0,1,18,10,0,1,18,10,0
  //   ,1,18,10,0,1,18,10,0,1,18,10,0,1,18,10,0,1,18,10,0,1,18,10,0,1
  //   ,18,10,0,1,18,10,0,1,18,10,0,1,18,10,0,1,18,10,0,1,18,10,0,1,18
  //   ,10,0,1,18,10,0,1,18,10,0,1,18,10,0,1,18,10,0,1,18,10,0,1,18,10
  //   ,0,1,18,10,0,1,18,10,0,1,18,10,0,1,18,10,0,1,18,10,0,1,18,10,0
  //   ,1,18,10,0,1,18,10,0,1,18,10,0,1,18,10,0,1,18,10,0,1,18,10,0,1
  //   ,18,10,0,1,18,10,0,1,18,10,0,1,18,10,0,1,18,10,0,1,18,10,0,1,18
  //   ,10,0,1,18,10,0,1,18,10,0,1,18,10,0,1,18,10,0,1,18,10,0,1,18,10
  //   ,0,1,18,10,0,1,18,10,0,1,18,10,0,1,18,10,0,1,18,10,0,1,18,10,0
  //   ,1,18,10,0,1,18,10,0,1,18,10,0,1,18,10,0,1,18,10,0,1,18,10,0,1
  //   ,18,10,0,1,18,10,0,1,18,10,0,1,18,10,0,1,18,10,0,1,18,10,0,1,18
  //   ,10,0,1,18,10,0,1,18,10,0,1,18,10,0,1,18,10,0,1,18,10,0,1,18,10
  //   ,0,1,18,10,0,1,18,10,0,1,18,10,0,1,18,10,0,1,18,10,0,1,18,10,0
  //   ,1,18,10,0,1,18,10,0,1,18,10,0,1,18,10,0,1,18,10,0,1,18,10,0,1
  //   ,18,10,0,1,18,10,0,1,18,10,0,1,18,10,0,1,18,10,0,1,18,10,0,1,18
  //   ,10,0,1,18,10,0,1,18,10,0,1,18,10,0,1,18,10,0,1,18,10,0,1,18,10
  //   ,0,1,18,10,0,1,18,10,0,1,18,10,0,1,18,10,0,1,18,10,0,1,18,10,0
  //   ,1,18,10,0,1,18,10,0,1,18,10,0,1,18,10,0,1,18,10,0,1,18,10,0,1
  //   ,18,10,0,1,18,10,0,1,18,10,0,1,18,10,0,1,18,10,0,1,18,10,0,1,18
  //   ,10,0,1,18,10,0,1,18,10,0,1,18,10,0,1,18,10,0,1,18,10,0,1,18,10
  //   ,0,1,18,10,0,1,18,10,0,1,18,10,0,1,18,10,0,1,18,10,0,1,18,10,0
  //   ,1,18,10,0,1,18,10,0,1,18,10,0,1,18,10,0,1,18,10,0,1,18,10,0,1
  //   ,18,10,0,1,18,10,0,1,18,10,0,1,18,10,0,1,18,10,0,1,18,10,0,1,18
  //   ,10,0,1,18,10,0,1,18,10,0,1,18,10,0,1,18,10,0,1,18,10,0,1,18,10
  //   ,0,1,18,10,0,1,18,10,0,1,18,10,0,1,18,10,0,1,18,10,0,1,18,10,0
  //   ,1,18,10,0,1,18,10,0,1,18,10,0,1,18,10,0,1,18,10,0,1,18,10,0,1
  //   ,18,10,0,1,18,10,0,1,18,10,0,1,18,10,0,1,18,10,0,1,18,10,0,1,18
  //   ,10,0,1,18,10,0,1,18,10,0,1,18,10,0,1,18,10,0,1,18,10,0,1,18,10
  //   ,0,1,18,10,0,1,18,10,0,1,18,10,0,1,18,10,0,1,18,10,0,1,18,10,0
  //   ,1,18,10,0,1,18,10,0,1,18,10,0,1,18,10,0,1,18,10,0,1,18,10,0,1
  //   ,18,10,0,1,18,10,0,1,18,10,0,1,18,10,0,1,18,10,0,1,18,10,0,1,18
  //   ,10,0,1,18,10,0,1,18,10,0,1,18,10,0,1,18,10,0,1,18,10,0,1,18,10
  //   ,0,1,18,10,0,1,18,10,0,1,18,10,0,1,18,10,0,1,18,10,0,1,18,10,0
  //   ,1,18,10,0,1,18,10,0,1,18,10,0,1,18,10,0,1,18,10,0,1,18,10,0,1
  //   ,18,10,0,1,18,10,0,1,18,10,0,1,18,10,0,1,18,10,0,1,18,10,0,1,18
  //   ,10,0,1,18,10,0,1,18,10,0,1,18,10,0,1,18,10,0,1,18,10,0,1,18,10
  //   ,0,1,18,10,0,1,18,10,0,1,18,10,0,1,18,10,0,1,18,10,0,1,18,10,0
  //   ,1,18,10,0,1,18,10,0,1,18,10,0,1,18,10,0,1,18,10,0,1,18,10,0,1
  //   ,18,10,0,1,18,10,0,1,18,10,0,1,18,10,0,1,18,10,0,1,18,10,0,1,18
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  //   UV Register
  //   IRs
  //   Registers
  //   ALU & Shift
  //   Flags
endmodule
