// Digital circuit main_pc.dig as structural Verilog
module main_pc (
  input  C,
  output [15:0] A_bus,
  output m_we,
  output m_oe
);

  wire addr_pc, addr_uv, addr_xy, and_1_out, bus_transceiver_1_p1, carry, clk_v, clk_y, cond, cond_upc_clr,
       demultiplexer_1_out_0, demultiplexer_1_out_1, demultiplexer_1_out_2, demultiplexer_1_out_3,
       demultiplexer_1_out_4, demultiplexer_1_out_5, demultiplexer_1_out_6, demultiplexer_1_out_7,
       demultiplexer_1_out_8, demultiplexer_1_out_9, demultiplexer_1_out_10, demultiplexer_1_out_11,
       demultiplexer_1_out_12, demultiplexer_1_out_13, demultiplexer_1_out_14, demultiplexer_2_out_1,
       demultiplexer_2_out_2, demultiplexer_2_out_3, demultiplexer_2_out_4, demultiplexer_2_out_5,
       demultiplexer_2_out_6, demultiplexer_2_out_7, demultiplexer_2_out_8, demultiplexer_2_out_9,
       demultiplexer_2_out_10, demultiplexer_2_out_11, demultiplexer_2_out_12, demultiplexer_2_out_13,
       demultiplexer_2_out_14, dst_a, dst_b, dst_u, dst_v, dst_x, dst_y, f_c, f_z, flags_we, io_oe, io_we,
       ir0_rd, ir1_rd, kb_oe, keyboard_1_av, multiplexer_1_out, not_1_out, or_1_out, or_2_out, pc_imm,
       pc_inc, pc_rd, pc_uv, pc_xy, ram_oe, ram_we, rom_oe, src_a, src_alu, src_b, src_external, src_imm8,
       src_shr, src_u, src_v, src_x, src_y, tm_we, upc_clr, V_ovf, Y_ovf, zero;
  wire [1:0] alu_op, pc_src, src_addr, uPC_out;
  wire [2:0] dst_data;
  wire [3:0] src_data;
  wire [3:2] op;
  wire [7:0] a_cont, alu_1_s, b_cont, d, driver_7_out, imm8, ir0_raw, ir1_raw;
  wire [7:6] rom_4_d;
  wire [11:0] imm12;
  wire [15:0] driver_1_out, pc_content, UV, XY;
  wire [15:8] keyboard_1_d;

  and and_1 (and_1_out, not_1_out, cond_upc_clr);
  not not_1 (not_1_out, cond);
  Decoder #(.Selector_Bits(2)) decoder_1 (.sel(pc_src), .out_0(pc_xy), .out_1(pc_uv), .out_2(pc_imm));  // open: out_3
  or or_1 (or_1_out, and_1_out, upc_clr);
  RAMDualPort #(.AddrBits(12), .Bits(8)) ramdualport_1 (
    .A(A_bus[11:0]), .Din(d), .str(ram_we), .C(C), .ld(ram_oe), .D(d));
  Counter #(.Bits(2)) uPC (.en(1'b1), .C(C), .clr(or_1_out), .out(uPC_out));  // open: ovf
  ROM #(.AddrBits(18), .Bits(8)) rom_1 (.A({op, alu_op, imm12, uPC_out}), .sel(1'b1), .D({m_oe, dst_data, src_data}));
  ROM #(.AddrBits(18), .Bits(8)) rom_2 (
    .A({op, alu_op, imm12, uPC_out}), .sel(1'b1), .D({ir0_rd, pc_src, pc_rd, pc_inc, src_addr, m_we}));
  ROM #(.AddrBits(12), .Bits(8)) rom_3 (.A(A_bus[11:0]), .sel(rom_oe), .D(d));
  Keyboard keyboard_1 (.C(C), .en(kb_oe), .D({keyboard_1_d, d}), .av(keyboard_1_av));
  Terminal terminal_1 (.D(d), .C(C), .en(tm_we));
  or or_2 (or_2_out, pc_rd, pc_inc);
  assign driver_1_out = pc_uv ? UV : 16'bz;  // Driver driver_1
  assign driver_1_out = pc_xy ? XY : 16'bz;  // Driver driver_2
  assign driver_1_out = pc_imm ? {pc_content[15:12], imm12} : 16'bz;  // Driver driver_3
  Decoder #(.Selector_Bits(4)) decoder_2 (
    .sel(src_data), .out_1(src_a), .out_2(src_b), .out_3(src_x), .out_4(src_y), .out_5(src_u), .out_6(src_v),
    .out_7(src_alu), .out_8(src_shr), .out_9(src_imm8), .out_10(src_external));  // open: out_0, out_11, out_12, out_13, out_14, out_15
  // Probe on {keyboard_1_d, d}
  LED led_1 (.in(keyboard_1_av));
  CounterPreset #(.Bits(16)) PC (
    .en(or_2_out), .C(C), .dir(1'b0), .in(driver_1_out), .ld(pc_rd), .clr(1'b0), .out(pc_content));  // open: ovf
  ROM #(.AddrBits(18), .Bits(8)) rom_4 (
    .A({op, alu_op, imm12, uPC_out}), .sel(1'b1),
    .D({rom_4_d, cond_upc_clr, upc_clr, flags_we, clk_v, clk_y, ir1_rd}));
  Decoder #(.Selector_Bits(2)) decoder_3 (
    .sel(src_addr), .out_0(addr_pc), .out_1(addr_xy), .out_2(addr_uv));  // open: out_3
  // Probe on {ir1_raw, ir0_raw}
  // Probe on d
  // Probe on A_bus[11:0]
  LED led_2 (.in(rom_oe));
  LED led_3 (.in(ram_oe));
  assign A_bus = addr_pc ? pc_content : 16'bz;  // Driver driver_4
  assign A_bus = addr_xy ? XY : 16'bz;  // Driver driver_5
  Decoder #(.Selector_Bits(3)) decoder_4 (
    .sel(dst_data), .out_1(dst_a), .out_2(dst_b), .out_3(dst_x), .out_4(dst_y), .out_5(dst_u), .out_6(dst_v));  // open: out_0, out_7
  LED led_4 (.in(demultiplexer_1_out_14));
  LED led_5 (.in(demultiplexer_1_out_13));
  LED led_6 (.in(demultiplexer_1_out_12));
  LED led_7 (.in(demultiplexer_1_out_11));
  or or_3 (ram_we, demultiplexer_1_out_1, demultiplexer_1_out_2, demultiplexer_1_out_3, demultiplexer_1_out_4, demultiplexer_1_out_5, demultiplexer_1_out_6, demultiplexer_1_out_7, demultiplexer_1_out_8, demultiplexer_1_out_9, demultiplexer_1_out_10);
  LED led_8 (.in(demultiplexer_1_out_0));
  LED led_9 (.in(demultiplexer_2_out_14));
  LED led_10 (.in(demultiplexer_2_out_13));
  LED led_11 (.in(demultiplexer_2_out_12));
  LED led_12 (.in(demultiplexer_2_out_11));
  or or_4 (ram_oe, demultiplexer_2_out_1, demultiplexer_2_out_2, demultiplexer_2_out_3, demultiplexer_2_out_4, demultiplexer_2_out_5, demultiplexer_2_out_6, demultiplexer_2_out_7, demultiplexer_2_out_8, demultiplexer_2_out_9, demultiplexer_2_out_10);
  assign A_bus = addr_uv ? UV : 16'bz;  // Driver driver_6
  LED led_13 (.in(kb_oe));
  CounterPreset #(.Bits(8)) V (
    .en(clk_v), .C(C), .dir(1'b0), .in(driver_7_out), .ld(dst_v), .clr(1'b0), .out(UV[7:0]), .ovf(V_ovf));
  CounterPreset #(.Bits(8)) U (
    .en(V_ovf), .C(C), .dir(1'b0), .in(driver_7_out), .ld(dst_u), .clr(1'b0), .out(UV[15:8]));  // open: ovf
  decoder decoder_5 (.b0(ir0_raw), .b1(ir1_raw), .op({op, alu_op}), .imm_12(imm12), .imm_8(imm8));
  Register #(.Bits(8)) register_1 (.D(driver_7_out), .C(C), .en(ir1_rd), .Q(ir1_raw));
  Register #(.Bits(8)) register_2 (.D(driver_7_out), .C(C), .en(ir0_rd), .Q(ir0_raw));
  Demultiplexer #(.Selector_Bits(4)) demultiplexer_1 (
    .sel(A_bus[15:12]), .in(m_we), .out_0(demultiplexer_1_out_0), .out_1(demultiplexer_1_out_1),
    .out_2(demultiplexer_1_out_2), .out_3(demultiplexer_1_out_3), .out_4(demultiplexer_1_out_4),
    .out_5(demultiplexer_1_out_5), .out_6(demultiplexer_1_out_6), .out_7(demultiplexer_1_out_7),
    .out_8(demultiplexer_1_out_8), .out_9(demultiplexer_1_out_9), .out_10(demultiplexer_1_out_10),
    .out_11(demultiplexer_1_out_11), .out_12(demultiplexer_1_out_12), .out_13(demultiplexer_1_out_13),
    .out_14(demultiplexer_1_out_14), .out_15(io_we));
  Demultiplexer #(.Selector_Bits(4)) demultiplexer_2 (
    .sel(A_bus[15:12]), .in(m_oe), .out_0(rom_oe), .out_1(demultiplexer_2_out_1),
    .out_2(demultiplexer_2_out_2), .out_3(demultiplexer_2_out_3), .out_4(demultiplexer_2_out_4),
    .out_5(demultiplexer_2_out_5), .out_6(demultiplexer_2_out_6), .out_7(demultiplexer_2_out_7),
    .out_8(demultiplexer_2_out_8), .out_9(demultiplexer_2_out_9), .out_10(demultiplexer_2_out_10),
    .out_11(demultiplexer_2_out_11), .out_12(demultiplexer_2_out_12), .out_13(demultiplexer_2_out_13),
    .out_14(demultiplexer_2_out_14), .out_15(io_oe));
  assign driver_7_out = src_v ? UV[7:0] : 8'bz;  // Driver driver_7
  assign driver_7_out = src_u ? UV[15:8] : 8'bz;  // Driver driver_8
  // bus_transceiver bus_transceiver_1: pin names not known; wires that end beside it: bus_transceiver_1_p1, 1'b0, driver_7_out, d
  not not_2 (bus_transceiver_1_p1, src_external);
  assign driver_7_out = src_a ? a_cont : 8'bz;  // Driver driver_9
  assign driver_7_out = src_b ? b_cont : 8'bz;  // Driver driver_10
  assign driver_7_out = src_x ? XY[15:8] : 8'bz;  // Driver driver_11
  assign driver_7_out = src_y ? XY[7:0] : 8'bz;  // Driver driver_12
  assign driver_7_out = src_imm8 ? imm8 : 8'bz;  // Driver driver_13
  Register #(.Bits(8)) A (.D(driver_7_out), .C(C), .en(dst_a), .Q(a_cont));
  Register #(.Bits(8)) B (.D(driver_7_out), .C(C), .en(dst_b), .Q(b_cont));
  CounterPreset #(.Bits(8)) X (
    .en(Y_ovf), .C(C), .dir(1'b0), .in(driver_7_out), .ld(dst_x), .clr(1'b0), .out(XY[15:8]));  // open: ovf
  CounterPreset #(.Bits(8)) Y (
    .en(clk_y), .C(C), .dir(1'b0), .in(driver_7_out), .ld(dst_y), .clr(1'b0), .out(XY[7:0]), .ovf(Y_ovf));
  Demultiplexer #(.Selector_Bits(4)) demultiplexer_3 (
    .sel(A_bus[3:0]), .in(io_we), .out_1(tm_we));  // open: out_0, out_2, out_3, out_4, out_5, out_6, out_7, out_8, out_9, out_10, out_11, out_12, out_13, out_14, out_15
  Demultiplexer #(.Selector_Bits(4)) demultiplexer_4 (
    .sel(A_bus[3:0]), .in(io_oe), .out_0(kb_oe));  // open: out_1, out_2, out_3, out_4, out_5, out_6, out_7, out_8, out_9, out_10, out_11, out_12, out_13, out_14, out_15
  assign driver_7_out = src_alu ? alu_1_s : 8'bz;  // Driver driver_14
  assign driver_7_out = src_shr ? {1'b0, a_cont[7:1]} : 8'bz;  // Driver driver_15
  Multiplexer multiplexer_1 (.sel(src_shr), .in_0(carry), .in_1(a_cont[0]), .out(multiplexer_1_out));
  Multiplexer multiplexer_2 (.sel(alu_op[0]), .in_0(f_z), .in_1(f_c), .out(cond));
  alu alu_1 (.b(b_cont), .a(a_cont), .op(alu_op), .s(alu_1_s), .c(carry), .z(zero));
  D_FF d_ff_1 (.D(zero), .C(flags_we), .Q(f_z));  // open: nQ
  D_FF d_ff_2 (.D(multiplexer_1_out), .C(flags_we), .Q(f_c));  // open: nQ

  // Other names for the same wires on the sheet: mem_oe = m_oe; mem_we = m_we; addr[11:0] = A_bus[11:0];
  //   sel[3:0] = A_bus[15:12]; shr_c = a_cont[0]; op[1:0] = alu_op

  // Notes on the sheet:
  //   C: Hz: 2147483647
  //   Microcode
  //   PC & Address Bus
  //   contents of rom_1 (hex, n*v repeats v):
  //   8a,8a,17,0,8a,8a,17,0,8a,8a,17,0,8a,8a,17,0,8a,8a,17,0,8a,8a,17
  //   ,0,8a,8a,17,0,8a,8a,17,0,8a,8a,17,0,8a,8a,17,0,8a,8a,17,0,8a,8a
  //   ,17,0,8a,8a,17,0,8a,8a,17,0,8a,8a,17,0,8a,8a,17,0,8a,8a,17,0,8a,8a
  //   ,17,0,8a,8a,17,0,8a,8a,17,0,8a,8a,17,0,8a,8a,17,0,8a,8a,17,0,8a,8a
  //   ,17,0,8a,8a,17,0,8a,8a,17,0,8a,8a,17,0,8a,8a,17,0,8a,8a,17,0,8a,8a
  //   ,17,0,8a,8a,17,0,8a,8a,17,0,8a,8a,17,0,8a,8a,17,0,8a,8a,17,0,8a,8a
  //   ,17,0,8a,8a,17,0,8a,8a,17,0,8a,8a,17,0,8a,8a,17,0,8a,8a,17,0,8a,8a
  //   ,17,0,8a,8a,17,0,8a,8a,17,0,8a,8a,17,0,8a,8a,17,0,8a,8a,17,0,8a,8a
  //   ,17,0,8a,8a,17,0,8a,8a,17,0,8a,8a,17,0,8a,8a,17,0,8a,8a,17,0,8a,8a
  //   ,17,0,8a,8a,17,0,8a,8a,17,0,8a,8a,17,0,8a,8a,17,0,8a,8a,17,0,8a,8a
  //   ,17,0,8a,8a,17,0,8a,8a,17,0,8a,8a,17,0,8a,8a,17,0,8a,8a,17,0,8a,8a
  //   ,17,0,8a,8a,17,0,8a,8a,17,0,8a,8a,17,0,8a,8a,17,0,8a,8a,17,0,8a,8a
  //   ,17,0,8a,8a,17,0,8a,8a,17,0,8a,8a,17,0,8a,8a,17,0,8a,8a,17,0,8a,8a
  //   ,17,0,8a,8a,17,0,8a,8a,17,0,8a,8a,17,0,8a,8a,17,0,8a,8a,17,0,8a,8a
  //   ,17,0,8a,8a,17,0,8a,8a,17,0,8a,8a,17,0,8a,8a,17,0,8a,8a,17,0,8a,8a
  //   ,17,0,8a,8a,17,0,8a,8a,17,0,8a,8a,17,0,8a,8a,17,0,8a,8a,17,0,8a,8a
  //   ,17,0,8a,8a,17,0,8a,8a,17,0,8a,8a,17,0,8a,8a,17,0,8a,8a,17,0,8a,8a
  //   ,17,0,8a,8a,17,0,8a,8a,17,0,8a,8a,17,0,8a,8a,17,0,8a,8a,17,0,8a,8a
  //   ,17,0,8a,8a,17,0,8a,8a,17,0,8a,8a,17,0,8a,8a,17,0,8a,8a,17,0,8a,8a
  //   ,17,0,8a,8a,17,0,8a,8a,17,0,8a,8a,17,0,8a,8a,17,0,8a,8a,17,0,8a,8a
  //   ,17,0,8a,8a,17,0,8a,8a,17,0,8a,8a,17,0,8a,8a,17,0,8a,8a,17,0,8a,8a
  //   ,17,0,8a,8a,17,0,8a,8a,17,0,8a,8a,17,0,8a,8a,17,0,8a,8a,17,0,8a,8a
  //   ,17,0,8a,8a,17,0,8a,8a,17,0,8a,8a,17,0,8a,8a,17,0,8a,8a,17,0,8a,8a
  //   ,17,0,8a,8a,17,0,8a,8a,17,0,8a,8a,17,0,8a,8a,17,0,8a,8a,17,0,8a,8a
  //   ,17,0,8a,8a,17,0,8a,8a,17,0,8a,8a,17,0,8a,8a,17,0,8a,8a,17,0,8a,8a
  //   ,17,0,8a,8a,17,0,8a,8a,17,0,8a,8a,17,0,8a,8a,17,0,8a,8a,17,0,8a,8a
  //   ,17,0,8a,8a,17,0,8a,8a,17,0,8a,8a,17,0,8a,8a,17,0,8a,8a,17,0,8a,8a
  //   ,17,0,8a,8a,17,0,8a,8a,17,0,8a,8a,17,0,8a,8a,17,0,8a,8a,17,0,8a,8a
  //   ,17,0,8a,8a,17,0,8a,8a,17,0,8a,8a,17,0,8a,8a,17,0,8a,8a,17,0,8a,8a
  //   ,17,0,8a,8a,17,0,8a,8a,17,0,8a,8a,17,0,8a,8a,17,0,8a,8a,17,0,8a,8a
  //   ,17,0,8a,8a,17,0,8a,8a,17,0,8a,8a,17,0,8a,8a,17,0,8a,8a,17,0,8a,8a
  //   ,17,0,8a,8a,17,0,8a,8a,17,0,8a,8a,17,0,8a,8a,17,0,8a,8a,17,0,8a,8a
  //   ,17,0,8a,8a,17,0,8a,8a,17,0,8a,8a,17,0,8a,8a,17,0,8a,8a,17,0,8a,8a
  //   ,17,0,8a,8a,17,0,8a,8a,17,0,8a,8a,17,0,8a,8a,17,0,8a,8a,17,0,8a,8a
  //   ,17,0,8a,8a,17,0,8a,8a,17,0,8a,8a,17,0,8a,8a,17,0,8a,8a,17,0,8a,8a
  //   ,17,0,8a,8a,17,0,8a,8a,17,0,8a,8a,17,0,8a,8a,17,0,8a,8a,17,0,8a,8a
  //   ,17,0,8a,8a,17,0,8a,8a,17,0,8a,8a,17,0,8a,8a,17,0,8a,8a,17,0,8a,8a
  //   ,17,0,8a,8a,17,0,8a,8a,17,0,8a,8a,17,0,8a,8a,17,0,8a,8a,17,0,8a,8a
  //   ,17,0,8a,8a,17,0,8a,8a,17,0,8a,8a,17,0,8a,8a,17,0,8a,8a,17,0,8a,8a
  //   ,17,0,8a,8a,17,0,8a,8a,17,0,8a,8a,17,0,8a,8a,17,0,8a,8a,17,0,8a,8a
  //   ,17,0,8a,8a,17,0,8a,8a,17,0,8a,8a,17,0,8a,8a,17,0,8a,8a,17,0,8a,8a
  //   ,17,0,8a,8a,17,0,8a,8a,17,0,8a,8a,17,0,8a,8a,17,0,8a,8a,17,0,8a,8a
  //   ,17,0,8a,8a,17,0,8a,8a,17,0,8a,8a,17,0,8a,8a,17,0,8a,8a,17,0,8a,8a
  //   ,17,0,8a,8a,17,0,8a,8a,17,0,8a,8a,17,0,8a,8a,17,0,8a,8a,17,0,8a,8a
  //   ,17,0,8a,8a,17,0,8a,8a,17,0,8a,8a,17,0,8a,8a,17,0,8a,8a,17,0,8a,8a
  //   ,17,0,8a,8a,17,0,8a,8a,17,0,8a,8a,17,0,8a,8a,17,0,8a,8a,17,0,8a,8a
  //   ,17,0,8a,8a,17,0,8a,8a,17,0,8a,8a,17,0,8a,8a,17,0,8a,8a,17,0,8a,8a
  //   ,17,0,8a,8a,17,0,8a,8a,17,0,8a,8a,17,0,8a,8a,17,0,8a,8a,17,0,8a,8a
  //   ,17,0,8a,8a,17,0,8a,8a,17,0,8a,8a,17,0,8a,8a,17,0,8a,8a,17,0,8a,8a
  //   ,17,0,8a,8a,17,0,8a,8a,17,0,8a,8a,17,0,8a,8a,17,0,8a,8a,17,0,8a,8a
  //   ,17,0,8a,8a,17,0,8a,8a,17,0,8a,8a,17,0,8a,8a,17,0,8a,8a,17,0,8a,8a
  //   ,17,0,8a,8a,17,0,8a,8a,17,0,8a,8a,17,0,8a,8a,17,0,8a,8a,17,0,8a,8a
  //   ,17,0,8a,8a,17,0,8a,8a,17,0,8a,8a,17,0,8a,8a,17,0,8a,8a,17,0,8a,8a
  //   ,17,0,8a,8a,17,0,8a,8a,17,0,8a,8a,17,0,8a,8a,17,0,8a,8a,17,0,8a,8a
  //   ,17,0,8a,8a,17,0,8a,8a,17,0,8a,8a,17,0,8a,8a,17,0,8a,8a,17,0,8a,8a
  //   ,17,0,8a,8a,17,0,8a,8a,17,0,8a,8a,17,0,8a,8a,17,0,8a,8a,17,0,8a,8a
  //   ,17,0,8a,8a,17,0,8a,8a,17,0,8a,8a,17,0,8a,8a,17,0,8a,8a,17,0,8a,8a
  //   ,17,0,8a,8a,17,0,8a,8a,17,0,8a,8a,17,0,8a,8a,17,0,8a,8a,17,0,8a,8a
  //   ,17,0,8a,8a,17,0,8a,8a,17,0,8a,8a,17,0,8a,8a,17,0,8a,8a,17,0,8a,8a
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  //   contents of rom_2 (hex, n*v repeats v):
  //   88,8,0,0,88,8,0,0,88,8,0,0,88,8,0,0,88,8,0,0,88,8,0,0,88,8,0,0
  //   ,88,8,0,0,88,8,0,0,88,8,0,0,88,8,0,0,88,8,0,0,88,8,0,0,88,8,0,0
  //   ,88,8,0,0,88,8,0,0,88,8,0,0,88,8,0,0,88,8,0,0,88,8,0,0,88,8,0,0
  //   ,88,8,0,0,88,8,0,0,88,8,0,0,88,8,0,0,88,8,0,0,88,8,0,0,88,8,0,0
  //   ,88,8,0,0,88,8,0,0,88,8,0,0,88,8,0,0,88,8,0,0,88,8,0,0,88,8,0,0
  //   ,88,8,0,0,88,8,0,0,88,8,0,0,88,8,0,0,88,8,0,0,88,8,0,0,88,8,0,0
  //   ,88,8,0,0,88,8,0,0,88,8,0,0,88,8,0,0,88,8,0,0,88,8,0,0,88,8,0,0
  //   ,88,8,0,0,88,8,0,0,88,8,0,0,88,8,0,0,88,8,0,0,88,8,0,0,88,8,0,0
  //   ,88,8,0,0,88,8,0,0,88,8,0,0,88,8,0,0,88,8,0,0,88,8,0,0,88,8,0,0
  //   ,88,8,0,0,88,8,0,0,88,8,0,0,88,8,0,0,88,8,0,0,88,8,0,0,88,8,0,0
  //   ,88,8,0,0,88,8,0,0,88,8,0,0,88,8,0,0,88,8,0,0,88,8,0,0,88,8,0,0
  //   ,88,8,0,0,88,8,0,0,88,8,0,0,88,8,0,0,88,8,0,0,88,8,0,0,88,8,0,0
  //   ,88,8,0,0,88,8,0,0,88,8,0,0,88,8,0,0,88,8,0,0,88,8,0,0,88,8,0,0
  //   ,88,8,0,0,88,8,0,0,88,8,0,0,88,8,0,0,88,8,0,0,88,8,0,0,88,8,0,0
  //   ,88,8,0,0,88,8,0,0,88,8,0,0,88,8,0,0,88,8,0,0,88,8,0,0,88,8,0,0
  //   ,88,8,0,0,88,8,0,0,88,8,0,0,88,8,0,0,88,8,0,0,88,8,0,0,88,8,0,0
  //   ,88,8,0,0,88,8,0,0,88,8,0,0,88,8,0,0,88,8,0,0,88,8,0,0,88,8,0,0
  //   ,88,8,0,0,88,8,0,0,88,8,0,0,88,8,0,0,88,8,0,0,88,8,0,0,88,8,0,0
  //   ,88,8,0,0,88,8,0,0,88,8,0,0,88,8,0,0,88,8,0,0,88,8,0,0,88,8,0,0
  //   ,88,8,0,0,88,8,0,0,88,8,0,0,88,8,0,0,88,8,0,0,88,8,0,0,88,8,0,0
  //   ,88,8,0,0,88,8,0,0,88,8,0,0,88,8,0,0,88,8,0,0,88,8,0,0,88,8,0,0
  //   ,88,8,0,0,88,8,0,0,88,8,0,0,88,8,0,0,88,8,0,0,88,8,0,0,88,8,0,0
  //   ,88,8,0,0,88,8,0,0,88,8,0,0,88,8,0,0,88,8,0,0,88,8,0,0,88,8,0,0
  //   ,88,8,0,0,88,8,0,0,88,8,0,0,88,8,0,0,88,8,0,0,88,8,0,0,88,8,0,0
  //   ,88,8,0,0,88,8,0,0,88,8,0,0,88,8,0,0,88,8,0,0,88,8,0,0,88,8,0,0
  //   ,88,8,0,0,88,8,0,0,88,8,0,0,88,8,0,0,88,8,0,0,88,8,0,0,88,8,0,0
  //   ,88,8,0,0,88,8,0,0,88,8,0,0,88,8,0,0,88,8,0,0,88,8,0,0,88,8,0,0
  //   ,88,8,0,0,88,8,0,0,88,8,0,0,88,8,0,0,88,8,0,0,88,8,0,0,88,8,0,0
  //   ,88,8,0,0,88,8,0,0,88,8,0,0,88,8,0,0,88,8,0,0,88,8,0,0,88,8,0,0
  //   ,88,8,0,0,88,8,0,0,88,8,0,0,88,8,0,0,88,8,0,0,88,8,0,0,88,8,0,0
  //   ,88,8,0,0,88,8,0,0,88,8,0,0,88,8,0,0,88,8,0,0,88,8,0,0,88,8,0,0
  //   ,88,8,0,0,88,8,0,0,88,8,0,0,88,8,0,0,88,8,0,0,88,8,0,0,88,8,0,0
  //   ,88,8,0,0,88,8,0,0,88,8,0,0,88,8,0,0,88,8,0,0,88,8,0,0,88,8,0,0
  //   ,88,8,0,0,88,8,0,0,88,8,0,0,88,8,0,0,88,8,0,0,88,8,0,0,88,8,0,0
  //   ,88,8,0,0,88,8,0,0,88,8,0,0,88,8,0,0,88,8,0,0,88,8,0,0,88,8,0,0
  //   ,88,8,0,0,88,8,0,0,88,8,0,0,88,8,0,0,88,8,0,0,88,8,0,0,88,8,0,0
  //   ,88,8,0,0,88,8,0,0,88,8,0,0,88,8,0,0,88,8,0,0,88,8,0,0,88,8,0,0
  //   ,88,8,0,0,88,8,0,0,88,8,0,0,88,8,0,0,88,8,0,0,88,8,0,0,88,8,0,0
  //   ,88,8,0,0,88,8,0,0,88,8,0,0,88,8,0,0,88,8,0,0,88,8,0,0,88,8,0,0
  //   ,88,8,0,0,88,8,0,0,88,8,0,0,88,8,0,0,88,8,0,0,88,8,0,0,88,8,0,0
  //   ,88,8,0,0,88,8,0,0,88,8,0,0,88,8,0,0,88,8,0,0,88,8,0,0,88,8,0,0
  //   ,88,8,0,0,88,8,0,0,88,8,0,0,88,8,0,0,88,8,0,0,88,8,0,0,88,8,0,0
  //   ,88,8,0,0,88,8,0,0,88,8,0,0,88,8,0,0,88,8,0,0,88,8,0,0,88,8,0,0
  //   ,88,8,0,0,88,8,0,0,88,8,0,0,88,8,0,0,88,8,0,0,88,8,0,0,88,8,0,0
  //   ,88,8,0,0,88,8,0,0,88,8,0,0,88,8,0,0,88,8,0,0,88,8,0,0,88,8,0,0
  //   ,88,8,0,0,88,8,0,0,88,8,0,0,88,8,0,0,88,8,0,0,88,8,0,0,88,8,0,0
  //   ,88,8,0,0,88,8,0,0,88,8,0,0,88,8,0,0,88,8,0,0,88,8,0,0,88,8,0,0
  //   ,88,8,0,0,88,8,0,0,88,8,0,0,88,8,0,0,88,8,0,0,88,8,0,0,88,8,0,0
  //   ,88,8,0,0,88,8,0,0,88,8,0,0,88,8,0,0,88,8,0,0,88,8,0,0,88,8,0,0
  //   ,88,8,0,0,88,8,0,0,88,8,0,0,88,8,0,0,88,8,0,0,88,8,0,0,88,8,0,0
  //   ,88,8,0,0,88,8,0,0,88,8,0,0,88,8,0,0,88,8,0,0,88,8,0,0,88,8,0,0
  //   ,88,8,0,0,88,8,0,0,88,8,0,0,88,8,0,0,88,8,0,0,88,8,0,0,88,8,0,0
  //   ,88,8,0,0,88,8,0,0,88,8,0,0,88,8,0,0,88,8,0,0,88,8,0,0,88,8,0,0
  //   ,88,8,0,0,88,8,0,0,88,8,0,0,88,8,0,0,88,8,0,0,88,8,0,0,88,8,0,0
  //   ,88,8,0,0,88,8,0,0,88,8,0,0,88,8,0,0,88,8,0,0,88,8,0,0,88,8,0,0
  //   ,88,8,0,0,88,8,0,0,88,8,0,0,88,8,0,0,88,8,0,0,88,8,0,0,88,8,0,0
  //   ,88,8,0,0,88,8,0,0,88,8,0,0,88,8,0,0,88,8,0,0,88,8,0,0,88,8,0,0
  //   ,88,8,0,0,88,8,0,0,88,8,0,0,88,8,0,0,88,8,0,0,88,8,0,0,88,8,0,0
  //   ,88,8,0,0,88,8,0,0,88,8,0,0,88,8,0,0,88,8,0,0,88,8,0,0,88,8,0,0
  //   ,88,8,0,0,88,8,0,0,88,8,0,0,88,8,0,0,88,8,0,0,88,8,0,0,88,8,0,0
  //   ,88,8,0,0,88,8,0,0,88,8,0,0,88,8,0,0,88,8,0,0,88,8,0,0,88,8,0,0
  //   ,88,8,0,0,88,8,0,0,88,8,0,0,88,8,0,0,88,8,0,0,88,8,0,0,88,8,0,0
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  //   contents of rom_3 (hex, n*v repeats v):
  //   40,10,50,0,40,0,60,0,40,2,80,0,c0,58,40,11,50,0,40,10,60,0,70
  //   ,0,90,0,b0,0,70,0,50,0,40,0,0,0,60,0,40,f0,95,0,40,1,96,0,40,0
  //   ,90,0,70,0,10,0,e0,3e,93,0,b0,0,c0,2e,40,11,50,0,40,0,60,0,70
  //   ,0,90,0,b0,0,70,0,50,0,40,0,0,0,60,0,d0,0,40,f0,50,0,40,0,60,0
  //   ,70,0,90,0,40,0,10,0,e0,58,40,10,50,0,40,1,60,0,40,0,0,0,80,0
  //   ,40,a,10,0,e1,0,40,8,10,0,e0,ce,40,10,50,0,40,0,60,0,70,0,90,0
  //   ,40,ff,10,0,e0,58,40,1,60,0,70,0,90,0,40,0,60,0,70,0,60,0,40,0,0,0
  //   ,80,0,40,f0,50,0,40,1,60,0,40,0,0,0,80,0,40,10,50,0,40,0,60,0
  //   ,70,0,90,0,40,1,0,0,80,0,c0,58,40,2,90,0,40,10,50,0,40,0,60,0
  //   ,70,0,10,0,e0,58,40,1,90,0,70,0,10,0,80,0,40,f0,50,0,40,1,60,0
  //   ,40,8,80,0,40,20,80,0,40,8,80,0,c0,58,40,f0,50,0,40,1,60,0,40
  //   ,d,80,0,40,a,80,0,40,10,50,0,40,0,60,0,70,0,90,0,40,2,10,0,e1
  //   ,24,c1,32,40,10,50,0,40,0,60,0,40,2,80,0,c0,58,40,10,50,0,40,1
  //   ,60,0,70,0,90,0,c1,51,55,6e,6b,6e,6f,77,6e,20,43,6f,6d,6d,61,6e
  //   ,64,21,0,40,11,50,0,40,10,60,0,40,40,80,0,b0,0,40,1,80,0,40,0
  //   ,60,0,40,73,80,0,b0,0,40,1,80,0,c0,e,c1,24
  //   contents of rom_4 (hex, n*v repeats v):
  //   0,1,18,10,0,1,18,10,0,1,18,10,0,1,18,10,0,1,18,10,0,1,18,10,0
  //   ,1,18,10,0,1,18,10,0,1,18,10,0,1,18,10,0,1,18,10,0,1,18,10,0,1
  //   ,18,10,0,1,18,10,0,1,18,10,0,1,18,10,0,1,18,10,0,1,18,10,0,1,18
  //   ,10,0,1,18,10,0,1,18,10,0,1,18,10,0,1,18,10,0,1,18,10,0,1,18,10
  //   ,0,1,18,10,0,1,18,10,0,1,18,10,0,1,18,10,0,1,18,10,0,1,18,10,0
  //   ,1,18,10,0,1,18,10,0,1,18,10,0,1,18,10,0,1,18,10,0,1,18,10,0,1
  //   ,18,10,0,1,18,10,0,1,18,10,0,1,18,10,0,1,18,10,0,1,18,10,0,1,18
  //   ,10,0,1,18,10,0,1,18,10,0,1,18,10,0,1,18,10,0,1,18,10,0,1,18,10
  //   ,0,1,18,10,0,1,18,10,0,1,18,10,0,1,18,10,0,1,18,10,0,1,18,10,0
  //   ,1,18,10,0,1,18,10,0,1,18,10,0,1,18,10,0,1,18,10,0,1,18,10,0,1
  //   ,18,10,0,1,18,10,0,1,18,10,0,1,18,10,0,1,18,10,0,1,18,10,0,1,18
  //   ,10,0,1,18,10,0,1,18,10,0,1,18,10,0,1,18,10,0,1,18,10,0,1,18,10
  //   ,0,1,18,10,0,1,18,10,0,1,18,10,0,1,18,10,0,1,18,10,0,1,18,10,0
  //   ,1,18,10,0,1,18,10,0,1,18,10,0,1,18,10,0,1,18,10,0,1,18,10,0,1
  //   ,18,10,0,1,18,10,0,1,18,10,0,1,18,10,0,1,18,10,0,1,18,10,0,1,18
  //   ,10,0,1,18,10,0,1,18,10,0,1,18,10,0,1,18,10,0,1,18,10,0,1,18,10
  //   ,0,1,18,10,0,1,18,10,0,1,18,10,0,1,18,10,0,1,18,10,0,1,18,10,0
  //   ,1,18,10,0,1,18,10,0,1,18,10,0,1,18,10,0,1,18,10,0,1,18,10,0,1
  //   ,18,10,0,1,18,10,0,1,18,10,0,1,18,10,0,1,18,10,0,1,18,10,0,1,18
  //   ,10,0,1,18,10,0,1,18,10,0,1,18,10,0,1,18,10,0,1,18,10,0,1,18,10
  //   ,0,1,18,10,0,1,18,10,0,1,18,10,0,1,18,10,0,1,18,10,0,1,18,10,0
  //   ,1,18,10,0,1,18,10,0,1,18,10,0,1,18,10,0,1,18,10,0,1,18,10,0,1
  //   ,18,10,0,1,18,10,0,1,18,10,0,1,18,10,0,1,18,10,0,1,18,10,0,1,18
  //   ,10,0,1,18,10,0,1,18,10,0,1,18,10,0,1,18,10,0,1,18,10,0,1,18,10
  //   ,0,1,18,10,0,1,18,10,0,1,18,10,0,1,18,10,0,1,18,10,0,1,18,10,0
  //   ,1,18,10,0,1,18,10,0,1,18,10,0,1,18,10,0,1,18,10,0,1,18,10,0,1
  //   ,18,10,0,1,18,10,0,1,18,10,0,1,18,10,0,1,18,10,0,1,18,10,0,1,18
  //   ,10,0,1,18,10,0,1,18,10,0,1,18,10,0,1,18,10,0,1,18,10,0,1,18,10
  //   ,0,1,18,10,0,1,18,10,0,1,18,10,0,1,18,10,0,1,18,10,0,1,18,10,0
  //   ,1,18,10,0,1,18,10,0,1,18,10,0,1,18,10,0,1,18,10,0,1,18,10,0,1
  //   ,18,10,0,1,18,10,0,1,18,10,0,1,18,10,0,1,18,10,0,1,18,10,0,1,18
  //   ,10,0,1,18,10,0,1,18,10,0,1,18,10,0,1,18,10,0,1,18,10,0,1,18,10
  //   ,0,1,18,10,0,1,18,10,0,1,18,10,0,1,18,10,0,1,18,10,0,1,18,10,0
  //   ,1,18,10,0,1,18,10,0,1,18,10,0,1,18,10,0,1,18,10,0,1,18,10,0,1
  //   ,18,10,0,1,18,10,0,1,18,10,0,1,18,10,0,1,18,10,0,1,18,10,0,1,18
  //   ,10,0,1,18,10,0,1,18,10,0,1,18,10,0,1,18,10,0,1,18,10,0,1,18,10
  //   ,0,1,18,10,0,1,18,10,0,1,18,10,0,1,18,10,0,1,18,10,0,1,18,10,0
  //   ,1,18,10,0,1,18,10,0,1,18,10,0,1,18,10,0,1,18,10,0,1,18,10,0,1
  //   ,18,10,0,1,18,10,0,1,18,10,0,1,18,10,0,1,18,10,0,1,18,10,0,1,18
  //   ,10,0,1,18,10,0,1,18,10,0,1,18,10,0,1,18,10,0,1,18,10,0,1,18,10
  //   ,0,1,18,10,0,1,18,10,0,1,18,10,0,1,18,10,0,1,18,10,0,1,18,10,0
  //   ,1,18,10,0,1,18,10,0,1,18,10,0,1,18,10,0,1,18,10,0,1,18,10,0,1
  //   ,18,10,0,1,18,10,0,1,18,10,0,1,18,10,0,1,18,10,0,1,18,10,0,1,18
  //   ,10,0,1,18,10,0,1,18,10,0,1,18,10,0,1,18,10,0,1,18,10,0,1,18,10
  //   ,0,1,18,10,0,1,18,10,0,1,18,10,0,1,18,10,0,1,18,10,0,1,18,10,0
  //   ,1,18,10,0,1,18,10,0,1,18,10,0,1,18,10,0,1,18,10,0,1,18,10,0,1
  //   ,18,10,0,1,18,10,0,1,18,10,0,1,18,10,0,1,18,10,0,1,18,10,0,1,18
  //   ,10,0,1,18,10,0,1,18,10,0,1,18,10,0,1,18,10,0,1,18,10,0,1,18,10
  //   ,0,1,18,10,0,1,18,10,0,1,18,10,0,1,18,10,0,1,18,10,0,1,18,10,0
  //   ,1,18,10,0,1,18,10,0,1,18,10,0,1,18,10,0,1,18,10,0,1,18,10,0,1
  //   ,18,10,0,1,18,10,0,1,18,10,0,1,18,10,0,1,18,10,0,1,18,10,0,1,18
  //   ,10,0,1,18,10,0,1,18,10,0,1,18,10,0,1,18,10,0,1,18,10,0,1,18,10
  //   ,0,1,18,10,0,1,18,10,0,1,18,10,0,1,18,10,0,1,18,10,0,1,18,10,0
  //   ,1,18,10,0,1,18,10,0,1,18,10,0,1,18,10,0,1,18,10,0,1,18,10,0,1
  //   ,18,10,0,1,18,10,0,1,18,10,0,1,18,10,0,1,18,10,0,1,18,10,0,1,18
  //   ,10,0,1,18,10,0,1,18,10,0,1,18,10,0,1,18,10,0,1,18,10,0,1,18,10
  //   ,0,1,18,10,0,1,18,10,0,1,18,10,0,1,18,10,0,1,18,10,0,1,18,10,0
  //   ,1,18,10,0,1,18,10,0,1,18,10,0,1,18,10,0,1,18,10,0,1,18,10,0,1
  //   ,18,10,0,1,18,10,0,1,18,10,0,1,18,10,0,1,18,10,0,1,18,10,0,1,18
  //   ,10,0,1,18,10,0,1,18,10,0,1,18,10,0,1,18,10,0,1,18,10,0,1,18,10
  //   ,0,1,18,10,0,1,18,10,0,1,18,10,0,1,18,10,0,1,18,10,0,1,18,10,0
  //   ,1,18,10,0,1,18,10,0,1,18,10,0,1,18,10,0,1,18,10,0,1,18,10,0,1
  //   ,18,10,0,1,18,10,0,1,18,10,0,1,18,10,0,1,18,10,0,1,18,10,0,1,18
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  //   UV Register
  //   IRs
  //   Registers
  //   ALU & Shift
  //   Flags
endmodule
